// Digital circuit frontpanel.dig as structural Verilog
module frontpanel (
  input  [15:0] A,
  input  [15:0] B,
  output [15:0] O
);

  wire decoder_1_p2, decoder_1_p3;

  // decoder decoder_1: pin names not known; wires that end beside it: {B, A}, decoder_1_p2, decoder_1_p3
  // execute execute_1: pin names not known; wires that end beside it: decoder_1_p2, decoder_1_p3, O
endmodule
